// Logisim project G2.circ as structural Verilog: 2 circuits, main circuit main
module main (
  input  in_1,
  output out_2,
  output [31:0] out_3,
  output out_4,
  output [1:0] out_5,
  output [15:0] out_6,
  output [3:0] out_7,
  output [5:0] out_8
);

  wire ALUSrc, clock_1_out, clock_2_out, RegDst, registerfile_1_p1, registerfile_1_p8, RegWrite;
  wire [4:0] multiplexer_1_out;
  wire [31:0] adder_1_p3, bit_extender_1_out, multiplexer_2_out, PC_q, registerfile_1_p9;

  Register #(.width(32)) PC (.D(adder_1_p3), .Q(PC_q), .clk(clock_1_out), .clr(in_1));  // open: en
  Clock clock_1 (.out(clock_1_out));
  // Adder adder_1: pin names not known; wires that end beside it: PC_q, 32'h4, adder_1_p3
  // MIPSProgramROM mipsprogramrom_1: pin names not known; wires that end beside it: PC_q, out_3
  // PLA Control: pin names not known; wires that end beside it: out_3[31:26]
  Multiplexer #(.width(5), .enable("false")) multiplexer_1 (
    .in0(out_3[20:16]), .in1(out_3[15:11]), .out(multiplexer_1_out), .sel(RegDst));
  Clock clock_2 (.out(clock_2_out));
  assign bit_extender_1_out = {{16{1'b0}}, out_3[15:0]};  // Bit_Extender bit_extender_1
  // RegisterFile registerfile_1: pin names not known; wires that end beside it: registerfile_1_p1, clock_2_out, RegWrite, multiplexer_1_out, out_3[25:21], out_3[20:16], in_1, registerfile_1_p8, registerfile_1_p9, registerfile_1_p9
  Multiplexer #(.width(32), .enable("false")) multiplexer_2 (
    .in0(registerfile_1_p9), .in1(bit_extender_1_out), .out(multiplexer_2_out), .sel(ALUSrc));
  // MIPS_ALU mips_alu_1: pin names not known; wires that end beside it: registerfile_1_p8, multiplexer_2_out, out_7, out_2, registerfile_1_p1, out_4
  ALUOp ALUOp (.ALUOp(out_5), .funct(out_3[5:0]), .ALU(out_7));
  // MIPSProgramROM mipsprogramrom_2: pin names not known

  assign out_6 = out_3[15:0];
  assign out_8 = out_3[5:0];

  // Other names for the same wires on the sheet: ALUOp[1:0] = out_5; Clear = in_1
endmodule

module ALUOp (
  input  [1:0] ALUOp,
  input  [5:0] funct,
  output [3:0] ALU
);

  // PLA pla_1: pin names not known; wires that end beside it: {ALUOp, funct}, ALU
endmodule
